# Fritzing sketch fritzing_sketch (saved by Fritzing 0.9.3b)
breadboards: 1

parts:
  Part1 = Arduino Mega 2560 (Rev3)
  S2 = Pushbutton [package="[THT]"]
  S3 = Pushbutton [package="[THT]"]
  S4 = Pushbutton [package="[THT]"]
  Part2 = Thumb Joystick
  S5 = Pushbutton [package="[THT]"]

nets:
  N1: Part1.A0, Part2.HORZ
  N2: Part1.A1, Part2.VERT
  N3: Part1.D13_PWM, Part2.SEL
  5V: Part1.5V, Part2.VCC
  GND: Part1.GND, S3.Pin_3, S3.Pin_4, S4.Pin_3, S4.Pin_4, Part2.GND
  N4: Part1.D2_PWM, S4.Pin_1, S4.Pin_2
  N5: Part1.D5_PWM, S3.Pin_1, S3.Pin_2
  N6: S2.Pin_1, S2.Pin_2, S2.Pin_3, S2.Pin_4
  N7: S5.Pin_1, S5.Pin_2, S5.Pin_3, S5.Pin_4
